// Logisim project relogio.circ as structural Verilog: 8 circuits, main circuit main
module main (
  input  in_1
);

  wire clock_1_out, decodificador4bin_0_9dec_1_a, decodificador4bin_0_9dec_1_b, decodificador4bin_0_9dec_1_c,
       decodificador4bin_0_9dec_1_d, decodificador4bin_0_9dec_1_e, decodificador4bin_0_9dec_1_f,
       decodificador4bin_0_9dec_1_out_11, undriven, undriven_2, undriven_3, undriven_4, undriven_5,
       undriven_6, undriven_7, undriven_8, undriven_9, undriven_10, undriven_11, undriven_12, undriven_13,
       undriven_14, undriven_15, undriven_16, undriven_17, undriven_18, undriven_19, undriven_20,
       undriven_21, undriven_22, undriven_23, undriven_24;

  decodificador4bin_0_9dec decodificador4bin_0_9dec_1 (
    .in_1(undriven), .in_2(undriven_2), .in_3(undriven_3), .in_4(undriven_4),
    .a(decodificador4bin_0_9dec_1_a), .b(decodificador4bin_0_9dec_1_b), .c(decodificador4bin_0_9dec_1_c),
    .d(decodificador4bin_0_9dec_1_d), .e(decodificador4bin_0_9dec_1_e), .f(decodificador4bin_0_9dec_1_f),
    .out_11(decodificador4bin_0_9dec_1_out_11));
  _7_Segment_Display u_7_segment_display_1 (
    .g(decodificador4bin_0_9dec_1_out_11), .f(decodificador4bin_0_9dec_1_f),
    .a(decodificador4bin_0_9dec_1_a), .b(decodificador4bin_0_9dec_1_b), .e(decodificador4bin_0_9dec_1_e),
    .d(decodificador4bin_0_9dec_1_d), .c(decodificador4bin_0_9dec_1_c));  // open: dp
  Clock clock_1 (.out(clock_1_out));
  decodificador4bin_0_9dec decodificador4bin_0_9dec_2 (
    .in_1(undriven_5), .in_2(undriven_6), .in_3(undriven_7), .in_4(undriven_8));  // open: a, b, c, d, e, f, out_11
  contador_completo contador_completo_1 (
    .PRESET(in_1), .VCC(clock_1_out), .in_2(undriven), .in_3(undriven_2), .in_4(undriven_3),
    .in_5(undriven_4), .in_6(undriven_5), .in_7(undriven_6), .in_8(undriven_7), .in_9(undriven_8),
    .in_10(undriven_9), .in_11(undriven_10), .in_12(undriven_11), .in_13(undriven_12), .in_14(undriven_18),
    .in_15(undriven_19), .in_16(undriven_20), .in_17(undriven_21), .in_18(undriven_13), .in_1(undriven_14),
    .in_19(undriven_15), .in_20(undriven_22), .in_21(undriven_16), .in_22(undriven_23), .in_23(undriven_17),
    .in_24(undriven_24));
  decodificador4bin_0_9dec decodificador4bin_0_9dec_3 (
    .in_1(undriven_9), .in_2(undriven_10), .in_3(undriven_11), .in_4(undriven_12));  // open: a, b, c, d, e, f, out_11
  decodificador4bin_0_9dec decodificador4bin_0_9dec_4 (
    .in_1(undriven_18), .in_2(undriven_19), .in_3(undriven_20), .in_4(undriven_21));  // open: a, b, c, d, e, f, out_11
  decodificador4bin_0_9dec decodificador4bin_0_9dec_5 (
    .in_1(undriven_13), .in_2(undriven_14), .in_3(undriven_15), .in_4(undriven_22));  // open: a, b, c, d, e, f, out_11
  decodificador4bin_0_9dec decodificador4bin_0_9dec_6 (
    .in_1(undriven_16), .in_2(undriven_23), .in_3(undriven_17), .in_4(undriven_24));  // open: a, b, c, d, e, f, out_11
endmodule

module contador4bits (
  input  PRESET,
  input  CLK,
  input  VCC,
  output out_4,
  output out_5,
  output out_6,
  output out_7,
  output out_8
);

  wire fliflopjk_1_out_7, fliflopjk_2_out_7, fliflopjk_3_out_7;

  and and_1 (out_8, out_7, fliflopjk_3_out_7, out_5, fliflopjk_1_out_7);
  fliflopjk fliflopjk_1 (
    .PRESET(PRESET), .J(VCC), .CLK(CLK), .K(VCC), .CLEAR(out_8), .out_6(out_4), .out_7(fliflopjk_1_out_7));
  fliflopjk fliflopjk_2 (
    .PRESET(PRESET), .J(VCC), .CLK(fliflopjk_1_out_7), .K(VCC), .CLEAR(out_8), .out_6(out_5),
    .out_7(fliflopjk_2_out_7));
  fliflopjk fliflopjk_3 (
    .PRESET(PRESET), .J(VCC), .CLK(fliflopjk_2_out_7), .K(VCC), .CLEAR(out_8), .out_6(out_6),
    .out_7(fliflopjk_3_out_7));
  fliflopjk fliflopjk_4 (
    .PRESET(PRESET), .J(VCC), .CLK(fliflopjk_3_out_7), .K(VCC), .CLEAR(out_8), .out_6(out_7));  // open: out_7

  // Notes on the sheet:
  //   out_7: pull=up
  //   PRESET: pull=up
  //   out_8: pull=up
  //   CLK: pull=up
  //   out_6: pull=up
  //   VCC: pull=up
  //   out_5: pull=up
  //   out_4: pull=up
endmodule

module fliflopjk (
  input  PRESET,
  input  J,
  input  CLK,
  input  K,
  input  CLEAR,
  output out_6,
  output out_7
);

  wire nand_1_out, nand_2_out, nand_3_out, nand_4_out, nand_5_out, nand_6_out, not_1_out, not_2_out,
       not_3_out, or_1_out;

  not not_1 (not_1_out, or_1_out);
  or or_1 (or_1_out, PRESET, CLEAR);
  not not_2 (not_2_out, CLK);
  nand nand_1 (nand_1_out, out_7, J, not_2_out);
  nand nand_2 (nand_2_out, not_2_out, K, out_6);
  nand nand_3 (nand_3_out, 1'b1, nand_1_out, nand_4_out);
  nand nand_4 (nand_4_out, nand_3_out, nand_2_out, not_1_out);
  nand nand_5 (nand_5_out, not_1_out, nand_3_out, not_3_out);
  not not_3 (not_3_out, not_2_out);
  nand nand_6 (nand_6_out, not_3_out, nand_4_out, 1'b1);
  nand nand_7 (out_6, 1'b1, nand_5_out, out_7);
  nand nand_8 (out_7, out_6, nand_6_out, not_1_out);

  // Notes on the sheet:
  //   out_7: pull=up
  //   CLEAR: pull=up
  //   out_6: pull=up
  //   CLK: pull=up
  //   K: pull=up
  //   J: pull=up
endmodule

module contador_completo (
  input  in_1,
  input  in_2,
  input  in_3,
  input  in_4,
  input  in_5,
  input  in_6,
  input  in_7,
  input  in_8,
  input  in_9,
  input  in_10,
  input  in_11,
  input  in_12,
  input  in_13,
  input  in_14,
  input  in_15,
  input  in_16,
  input  in_17,
  input  in_18,
  input  in_19,
  input  in_20,
  input  in_21,
  input  in_22,
  input  in_23,
  input  in_24,
  input  PRESET,
  input  VCC
);

  wire clock_1_out, contador4bits6_1_out_8, contador4bits6_2_out_8, contador4bits_1_out_8,
       contador4bits_2_out_8, counthourdec_1_soutforcount, hourcont_1_sout;

  Clock clock_1 (.out(clock_1_out));
  contador4bits contador4bits_1 (
    .out_8(contador4bits_1_out_8), .out_4(in_2), .out_5(in_3), .out_6(in_4), .out_7(in_5), .CLK(clock_1_out),
    .PRESET(PRESET), .VCC(VCC));
  contador4bits6 contador4bits6_1 (
    .PRESET(PRESET), .CLK(contador4bits_1_out_8), .VCC(VCC), .out_4(in_6), .out_5(in_7), .out_6(in_8),
    .out_7(in_9), .out_8(contador4bits6_1_out_8));
  contador4bits contador4bits_2 (
    .out_8(contador4bits_2_out_8), .out_4(in_10), .out_5(in_11), .out_6(in_12), .out_7(in_13),
    .CLK(contador4bits6_1_out_8), .PRESET(PRESET), .VCC(VCC));
  contador4bits6 contador4bits6_2 (
    .PRESET(PRESET), .CLK(contador4bits_2_out_8), .VCC(VCC), .out_4(in_14), .out_5(in_15), .out_6(in_16),
    .out_7(in_17), .out_8(contador4bits6_2_out_8));
  hourCont hourcont_1 (
    .PRESET(PRESET), .CLK(contador4bits6_2_out_8), .VCC(VCC), .Sin(counthourdec_1_soutforcount), .q1(in_18),
    .q2(in_1), .q3(in_19), .q4(in_20), .Sout(hourcont_1_sout));
  countHourDec counthourdec_1 (
    .PRESET(PRESET), .CLK(hourcont_1_sout), .VCC(VCC), .q1(in_21), .q2(in_22), .q3(in_23), .q4(in_24),
    .soutForCount(counthourdec_1_soutforcount));

  // Notes on the sheet:
  //   VCC: pull=up
  //   in_20: pull=up
  //   in_3: pull=up
  //   in_1: pull=up
  //   in_22: pull=up
  //   in_9: pull=up
  //   in_15: pull=up
  //   in_10: pull=up
  //   in_11: pull=up
  //   in_23: pull=up
  //   in_2: pull=up
  //   PRESET: pull=up
  //   in_7: pull=up
  //   in_16: pull=up
  //   in_6: pull=up
  //   in_12: pull=up
  //   in_14: pull=up
  //   in_18: pull=up
  //   in_13: pull=up
  //   in_24: pull=up
  //   in_21: pull=up
  //   in_4: pull=up
  //   in_8: pull=up
  //   in_17: pull=up
  //   in_19: pull=up
  //   in_5: pull=up
endmodule

module decodificador4bin_0_9dec (
  input  in_1,
  input  in_2,
  input  in_3,
  input  in_4,
  output a,
  output b,
  output c,
  output d,
  output e,
  output f,
  output out_11
);

  wire and_1_out, and_2_out, and_3_out, and_4_out, and_5_out, and_6_out, not_1_out, not_2_out, not_3_out,
       not_4_out;

  not not_1 (not_1_out, in_1);
  not not_2 (not_2_out, in_2);
  not not_3 (not_3_out, in_3);
  not not_4 (not_4_out, in_4);
  and and_1 (and_1_out, not_1_out, not_2_out, not_3_out);
  and and_2 (and_2_out, not_1_out, in_2, not_4_out);
  or or_1 (a, and_1_out, and_2_out, and_3_out);
  and and_3 (and_3_out, in_1, not_3_out, not_4_out);
  and and_4 (and_4_out, in_1, not_3_out, in_4);
  and and_5 (and_5_out, not_1_out, not_2_out, not_4_out);
  or or_2 (b, and_1_out, and_5_out, and_4_out);
  or or_3 (c, and_1_out, and_5_out, and_4_out);
  or or_4 (d, and_1_out, and_5_out, and_4_out);
  or or_5 (e, and_1_out, and_5_out, and_6_out);
  and and_6 (and_6_out, in_1, not_3_out, not_4_out);
  or or_6 (f, and_1_out, and_5_out, and_4_out);
  or or_7 (out_11, and_1_out, and_6_out);

  // Notes on the sheet:
  //   out_11: pull=up
  //   f: pull=up
  //   e: pull=up
  //   in_3: pull=up
  //   in_2: pull=up
  //   in_1: pull=up
  //   in_4: pull=up
  //   b: pull=up
  //   d: pull=up
  //   a: pull=up
  //   c: pull=up
endmodule

module contador4bits6 (
  input  PRESET,
  input  CLK,
  input  VCC,
  output out_4,
  output out_5,
  output out_6,
  output out_7,
  output out_8
);

  wire fliflopjk_1_out_7, fliflopjk_2_out_7, fliflopjk_3_out_7, fliflopjk_4_out_7;

  and and_1 (out_8, fliflopjk_4_out_7, out_5, out_6, fliflopjk_1_out_7);
  fliflopjk fliflopjk_1 (
    .PRESET(PRESET), .J(VCC), .CLK(CLK), .K(VCC), .CLEAR(out_8), .out_6(out_4), .out_7(fliflopjk_1_out_7));
  fliflopjk fliflopjk_2 (
    .PRESET(PRESET), .J(VCC), .CLK(fliflopjk_1_out_7), .K(VCC), .CLEAR(out_8), .out_6(out_5),
    .out_7(fliflopjk_2_out_7));
  fliflopjk fliflopjk_3 (
    .PRESET(PRESET), .J(VCC), .CLK(fliflopjk_2_out_7), .K(VCC), .CLEAR(out_8), .out_6(out_6),
    .out_7(fliflopjk_3_out_7));
  fliflopjk fliflopjk_4 (
    .PRESET(PRESET), .J(VCC), .CLK(fliflopjk_3_out_7), .K(VCC), .CLEAR(out_8), .out_6(out_7),
    .out_7(fliflopjk_4_out_7));

  // Notes on the sheet:
  //   PRESET: pull=up
  //   out_8: pull=up
  //   VCC: pull=up
  //   out_5: pull=up
  //   out_4: pull=up
  //   out_6: pull=up
  //   out_7: pull=up
  //   CLK: pull=up
endmodule

module hourCont (
  input  PRESET,
  input  CLK,
  input  VCC,
  input  Sin,
  output q1,
  output q2,
  output q3,
  output q4,
  output Sout
);

  wire and_1_out, and_2_out, fliflopjk_1_out_7, fliflopjk_2_out_7, fliflopjk_3_out_7, fliflopjk_4_out_7;

  and and_1 (and_1_out, q4, fliflopjk_3_out_7, q2, fliflopjk_1_out_7);
  fliflopjk fliflopjk_1 (
    .PRESET(PRESET), .J(VCC), .CLK(CLK), .K(VCC), .CLEAR(Sout), .out_6(q1), .out_7(fliflopjk_1_out_7));
  and and_2 (and_2_out, Sin, q2, q1, q2, fliflopjk_4_out_7);
  fliflopjk fliflopjk_2 (
    .PRESET(PRESET), .J(VCC), .CLK(fliflopjk_1_out_7), .K(VCC), .CLEAR(Sout), .out_6(q2),
    .out_7(fliflopjk_2_out_7));
  fliflopjk fliflopjk_3 (
    .PRESET(PRESET), .J(VCC), .CLK(fliflopjk_2_out_7), .K(VCC), .CLEAR(Sout), .out_6(q3),
    .out_7(fliflopjk_3_out_7));
  or or_1 (Sout, and_1_out, and_2_out);
  fliflopjk fliflopjk_4 (
    .PRESET(PRESET), .J(VCC), .CLK(fliflopjk_3_out_7), .K(VCC), .CLEAR(Sout), .out_6(q4),
    .out_7(fliflopjk_4_out_7));

  // Notes on the sheet:
  //   PRESET: pull=up
  //   q2: pull=up
  //   q1: pull=up
  //   VCC: pull=up
  //   q4: pull=up
  //   q3: pull=up
  //   Sout: pull=up
  //   CLK: pull=up
endmodule

module countHourDec (
  input  PRESET,
  input  CLK,
  input  VCC,
  output q1,
  output q2,
  output q3,
  output q4,
  output soutForCount
);

  wire and_1_out, fliflopjk_1_out_7, fliflopjk_2_out_7, fliflopjk_3_out_7, fliflopjk_4_out_7;

  and and_1 (and_1_out, fliflopjk_1_out_7, q2, fliflopjk_4_out_7, fliflopjk_3_out_7);
  and and_2 (soutForCount, q1, fliflopjk_2_out_7, fliflopjk_3_out_7, fliflopjk_4_out_7);
  fliflopjk fliflopjk_1 (
    .PRESET(PRESET), .J(VCC), .CLK(CLK), .K(VCC), .CLEAR(and_1_out), .out_6(q1), .out_7(fliflopjk_1_out_7));
  fliflopjk fliflopjk_2 (
    .PRESET(PRESET), .J(VCC), .CLK(fliflopjk_1_out_7), .K(VCC), .CLEAR(and_1_out), .out_6(q2),
    .out_7(fliflopjk_2_out_7));
  fliflopjk fliflopjk_3 (
    .PRESET(PRESET), .J(VCC), .CLK(fliflopjk_2_out_7), .K(VCC), .CLEAR(and_1_out), .out_6(q3),
    .out_7(fliflopjk_3_out_7));
  fliflopjk fliflopjk_4 (
    .PRESET(PRESET), .J(VCC), .CLK(fliflopjk_3_out_7), .K(VCC), .CLEAR(and_1_out), .out_6(q4),
    .out_7(fliflopjk_4_out_7));

  // Notes on the sheet:
  //   q4: pull=up
  //   PRESET: pull=up
  //   q3: pull=up
  //   q2: pull=up
  //   VCC: pull=up
  //   q1: pull=up
  //   soutForCount: pull=up
  //   CLK: pull=up
endmodule
